# Fritzing sketch AntiLog-MM_Unit_Test (saved by Fritzing 0.9.3b)
perfboards: 1
breadboards: 1

parts:
  J1 = female pin header, 2 pins [form="♀ (female)"]
  J2 = female pin header, 3 pins [form="♀ (female)"]  # not connected
  J3 = female pin header, 2 pins [form="♀ (female)"]  # not connected
  J5 = female pin header, 2 pins [form="♀ (female)"]  # not connected
  J6 = female pin header, 3 pins [form="♀ (female)"]  # not connected
  J7 = female pin header, 3 pins [form="♀ (female)"]
  R2 = Resistor [tolerance=±5% resistance=10k package=THT]

nets:
  N1: J1.pin2, R2.Pin_0
  N2: J7.pin3, R2.Pin_1

notes:
  AntiLog-MM
  (Current Sink)
  +/- 9V PSU
  AD9833
  FG
  RL
  Current
  <----
  PWR OUT
  OUT
