# Fritzing sketch TLF01+Antilog-MM_Test (saved by Fritzing 0.9.3b)
breadboards: 1
perfboards: 1

parts:
  Q1 = NPN-Transistor [package="TO92 [THT]"]
  Q2 = PNP-Transistor [package="TO92 [THT]"]
  R1 = Resistor [tolerance=±5% resistance=47k package=THT]
  R2 = Resistor [tolerance=±5% resistance=2.2k package=THT]
  R3 = Resistor [tolerance=±5% resistance=330 package=THT]
  R4 = Resistor [tolerance=±5% resistance=68k package=THT]
  C1 = Electrolytic Capacitor [capacitance=1µF package="100 mil [THT, electrolytic]"]
  R6 = TRIMPOT [package=trimpot_pth_s3_lock]
  J1 = female pin header, 2 pins [form="♀ (female)"]
  J2 = female pin header, 2 pins [form="♀ (female)"]  # not connected
  J3 = female pin header, 2 pins [form="♀ (female)"]
  J4 = female pin header, 3 pins [form="♀ (female)"]
  R7 = Resistor [tolerance=±5% resistance=680 package=THT]
  J5 = female pin header, 3 pins [form="♀ (female)"]
  J6 = female pin header, 3 pins [form="♀ (female)"]  # not connected
  J7 = female pin header, 2 pins [form="♀ (female)"]  # not connected
  R8 = Rotary Potentiometer (Small) [maximum_resistance=100kΩ package=THT]
  R9 = Resistor [tolerance=±5% resistance=47k package=THT]
  R11 = Resistor [tolerance=±5% resistance=47k package=THT]
  C2 = Electrolytic Capacitor [capacitance=1µF package="100 mil [THT, electrolytic]"]
  C3 = Ceramic Capacitor [capacitance=100nF package="100 mil [THT, multilayer]"]
  R12 = Rotary Potentiometer (Small) [maximum_resistance=100kΩ package=THT]
  R13 = Resistor [tolerance=±5% resistance=1k package=THT]
  LED1 = LED - 3mm [color="Green (570nm)" package="3 mm [THT]"]
  LED2 = LED - 3mm [color="Red (633nm)" package="3 mm [THT]"]
  R14 = Resistor [tolerance=±5% resistance=1k package=THT]

nets:
  N1: Q1.E, R2.Pin_1, C1.-, R6.CCW, J5.pin2, C2.+, C3.1, R13.Pin_0, LED2.cathode
  N2: Q1.B, R7.Pin_1
  N3: Q1.C, Q2.E, R4.Pin_1
  N4: Q2.B, R3.Pin_1
  N5: Q2.C, R1.Pin_0, R2.Pin_0, R9.Pin_0, R11.Pin_0, C3.0
  N6: R3.Pin_0, J5.pin3, C2.-, R12.leg1
  N7: R4.Pin_0, R6.WIPER
  N8: C1.+, R6.CW, J5.pin1, R12.leg2, R14.Pin_1
  N9: J1.pin1, R8.leg2
  N10: J1.pin2, R8.wiper
  N11: J3.pin1, R7.Pin_0
  N12: J4.pin2, J4.pin3
  N13: R11.Pin_1, R12.wiper
  N14: R13.Pin_1, LED1.anode
  N15: LED2.anode, R14.Pin_0

notes:
  Arduino LFO
  2SC1814 / 2SA1015
  E/C/B
  Antilog
  V->C Convertor
  (NPN+PNP)
  PCM5102A
  Function Generator
  +/-9V PSU
  GND
  +9V
  OUT
  Current Source
  Select
  (External)
  TLF01
  Q Ctrl
  10k / B
  -9V
  GND
  AD9833 FG
  10k/B
  POT
  10k Trim
