# Fritzing sketch Antilog_Diff_Unit_Test (saved by Fritzing 0.9.3b)
breadboards: 2

parts:
  IC1 = Dual Op-Amp [package=dip08]
  R1 = Resistor [tolerance=±5% resistance=100k package=THT]
  R2 = Resistor [tolerance=±5% resistance=100k package=THT]
  R5 = Resistor [tolerance=±5% resistance=1k package=THT]
  Q1 = NPN-Transistor [package="TO92 [THT]"]
  Q2 = NPN-Transistor [package="TO92 [THT]"]
  R6 = Resistor [tolerance=±5% resistance=68k package=THT]
  R7 = Resistor [tolerance=±5% resistance=330 package=THT]
  R8 = Resistor [tolerance=±5% resistance=1k package=THT]
  IC2 = Dual Op-Amp [package=dip08]
  C1 = Ceramic Capacitor [capacitance=100nF package="100 mil [THT, multilayer]"]
  C2 = Ceramic Capacitor [capacitance=100nF package="100 mil [THT, multilayer]"]
  C3 = Ceramic Capacitor [capacitance=100nF package="100 mil [THT, multilayer]"]
  C4 = Ceramic Capacitor [capacitance=100nF package="100 mil [THT, multilayer]"]
  C5 = Ceramic Capacitor [capacitance=100nF package="100 mil [THT, multilayer]"]
  C7 = Electrolytic Capacitor [capacitance=1µF package="100 mil [THT, electrolytic]"]
  R4 = Resistor [tolerance=±5% resistance=20k package=THT]
  C6 = Electrolytic Capacitor [capacitance=1µF package="100 mil [THT, electrolytic]"]
  R9 = Resistor [tolerance=±5% resistance=1k package=THT]

nets:
  N1: IC1.A_OUT, R1.Pin_0, R4.Pin_1
  N2: IC1.A_-IN, R1.Pin_1, R2.Pin_0
  N3: IC1.A_+IN, IC1.B_+IN, R5.Pin_1, Q2.C, IC2.A_+IN, IC2.B_+IN, C2.0, C3.0, C4.0, C5.0, C7.+, C6.-
  N4: IC1.A_V-, IC2.A_V-, C3.1, C5.1, C7.-
  N5: IC1.B_-IN, IC1.B_OUT
  N6: IC1.A_V+, R6.Pin_0, IC2.A_V+, C2.1, C4.1, C6.+, R9.Pin_1
  N7: R5.Pin_0, Q1.C, R4.Pin_0
  N8: Q1.E, Q2.E, R7.Pin_1
  N9: Q1.B, R6.Pin_1, IC2.B_-IN, C1.1
  N10: Q2.B, R8.Pin_0
  N11: R7.Pin_0, IC2.B_OUT, C1.0
  N12: R8.Pin_1, R9.Pin_0
  N13: IC2.A_OUT, IC2.A_-IN

notes:
  VEE
  GND
  GND
  VCC
  2SC1815
  E / C / B
  PCM5102A_FG
  RL
  Current ←
