# Fritzing sketch Antilog_Diff_Unit_Test2 (saved by Fritzing 0.9.3b)
breadboards: 2

parts:
  IC1 = Dual Op-Amp [package=dip08]
  R1 = Resistor [tolerance=±5% resistance=100k package=THT]
  R2 = Resistor [tolerance=±5% resistance=100k package=THT]
  R5 = Resistor [tolerance=±5% resistance=1k package=THT]
  Q1 = NPN-Transistor [package="TO92 [THT]"]
  Q2 = NPN-Transistor [package="TO92 [THT]"]
  R6 = Resistor [tolerance=±5% resistance=68k package=THT]
  R7 = Resistor [tolerance=±5% resistance=330 package=THT]
  R8 = Resistor [tolerance=±5% resistance=1k package=THT]
  C1 = Ceramic Capacitor [capacitance=100nF package="100 mil [THT, multilayer]"]
  C4 = Ceramic Capacitor [capacitance=100nF package="100 mil [THT, multilayer]"]
  C5 = Ceramic Capacitor [capacitance=100nF package="100 mil [THT, multilayer]"]
  C7 = Electrolytic Capacitor [capacitance=1µF package="100 mil [THT, electrolytic]"]
  C6 = Electrolytic Capacitor [capacitance=1µF package="100 mil [THT, electrolytic]"]
  R9 = Resistor [tolerance=±5% resistance=1k package=THT]
  R10 = Resistor [tolerance=±5% resistance=20k package=THT]

nets:
  N1: IC1.A_OUT, R1.Pin_0, R10.Pin_1
  N2: IC1.A_-IN, R1.Pin_1, R2.Pin_0
  N3: IC1.A_+IN, IC1.B_+IN, R5.Pin_1, C4.0, C5.0, C7.+, C6.-
  N4: IC1.A_V-, C5.1, C7.-
  N5: IC1.B_-IN, Q1.B, R6.Pin_1, C1.1
  N6: IC1.B_OUT, R7.Pin_0, C1.0
  N7: IC1.A_V+, R6.Pin_0, C4.1, C6.+, R9.Pin_1
  N8: R5.Pin_0, Q1.C, R10.Pin_0
  N9: Q1.E, Q2.E, R7.Pin_1
  N10: Q2.B, R8.Pin_0
  N11: R8.Pin_1, R9.Pin_0

notes:
  VEE
  GND
  GND
  VCC
  2SC1815
  E / C / B
  PCM5102A_FG
  RL
  Current ←
