# Fritzing sketch Antilog_NPNO (saved by Fritzing 0.9.3b)
breadboards: 2

parts:
  IC1 = Dual Op-Amp [package=dip08]
  R1 = Resistor [tolerance=±5% resistance=10k package=THT]
  R5 = Resistor [tolerance=±5% resistance=1k package=THT]
  Q1 = NPN-Transistor [package="TO92 [THT]"]
  Q2 = NPN-Transistor [package="TO92 [THT]"]
  R6 = Resistor [tolerance=±5% resistance=68k package=THT]
  R7 = Resistor [tolerance=±5% resistance=1k package=THT]
  R8 = Resistor [tolerance=±5% resistance=1k package=THT]
  C1 = Ceramic Capacitor [capacitance=100nF package="100 mil [THT, multilayer]"]
  C4 = Ceramic Capacitor [capacitance=100nF package="100 mil [THT, multilayer]"]
  C5 = Ceramic Capacitor [capacitance=100nF package="100 mil [THT, multilayer]"]
  C7 = Electrolytic Capacitor [capacitance=1µF package="100 mil [THT, electrolytic]"]
  C6 = Electrolytic Capacitor [capacitance=1µF package="100 mil [THT, electrolytic]"]
  R9 = Resistor [tolerance=±5% resistance=1k package=THT]
  R10 = Resistor [tolerance=±5% resistance=20k package=THT]
  R11 = TRIMPOT [package=trimpot_pth_s3_lock]
  R12 = Resistor [tolerance=±5% resistance=47k package=THT]
  R13 = Resistor [tolerance=±5% resistance=47k package=THT]
  R14 = Resistor [tolerance=±10% resistance=100k package=THT]
  R15 = Resistor [tolerance=±10% resistance=10k package=THT]
  R16 = Resistor [tolerance=±10% resistance=10k package=THT]
  R17 = Rotary Potentiometer (Small) [maximum_resistance=100kΩ package=THT]
  R18 = Resistor [tolerance=±5% resistance=10k package=THT]
  LED1 = LED - 3mm [color="Red (633nm)" package="3 mm [THT]"]
  R19 = Resistor [tolerance=±5% resistance=10k package=THT]
  LED2 = LED - 3mm [color="Blue (525nm)" package="3 mm [THT]"]

nets:
  N1: IC1.A_OUT, R1.Pin_0, R11.CCW
  N2: IC1.A_-IN, R1.Pin_1, R12.Pin_1, R13.Pin_1, R14.Pin_1
  N3: IC1.A_+IN, IC1.B_+IN, R5.Pin_1, Q2.C, C4.0, C5.0, C7.+, C6.-, LED1.cathode, LED2.anode
  N4: IC1.A_V-, C5.1, C7.-, R16.Pin_1, R19.Pin_1
  N5: IC1.B_-IN, Q1.B, R6.Pin_1, C1.1
  N6: IC1.B_OUT, R7.Pin_0, C1.0
  N7: IC1.A_V+, R6.Pin_0, C4.1, C6.+, R9.Pin_1, R15.Pin_0, R18.Pin_0
  N8: R5.Pin_0, Q1.C, R10.Pin_0
  N9: Q1.E, Q2.E, R7.Pin_1
  N10: Q2.B, R8.Pin_0
  N11: R8.Pin_1, R9.Pin_0
  N12: R10.Pin_1, R11.WIPER, R11.CW
  N13: R14.Pin_0, R17.wiper
  N14: R15.Pin_1, R17.leg2
  N15: R16.Pin_0, R17.leg1
  N16: R19.Pin_0, LED2.cathode

notes:
  VEE
  GND
  GND
  VCC
  2SC1815
  E / C / B
  RL
  Current ←
  LFO
  EG
  POT 10k/B
