# Fritzing sketch TLF01+Antilog_ Analog2.0 (saved by Fritzing 0.9.3b)
breadboards: 1
perfboards: 1

parts:
  IC1 = Dual Op-Amp [package=dip08]
  R1 = Resistor [tolerance=±5% resistance=100k package=THT]
  R2 = Resistor [tolerance=±5% resistance=100k package=THT]
  R5 = Resistor [tolerance=±5% resistance=1k package=THT]
  Q1 = NPN-Transistor [package="TO92 [THT]"]
  Q2 = NPN-Transistor [package="TO92 [THT]"]
  R6 = Resistor [tolerance=±5% resistance=68k package=THT]
  R7 = Resistor [tolerance=±5% resistance=330 package=THT]
  R8 = Resistor [tolerance=±5% resistance=1k package=THT]
  IC2 = Dual Op-Amp [package=dip08]
  C1 = Ceramic Capacitor [capacitance=100nF package="100 mil [THT, multilayer]"]
  C2 = Ceramic Capacitor [capacitance=100nF package="100 mil [THT, multilayer]"]
  C3 = Ceramic Capacitor [capacitance=100nF package="100 mil [THT, multilayer]"]
  C4 = Ceramic Capacitor [capacitance=100nF package="100 mil [THT, multilayer]"]
  C5 = Ceramic Capacitor [capacitance=100nF package="100 mil [THT, multilayer]"]
  C6 = Electrolytic Capacitor [capacitance=1µF package="100 mil [THT, electrolytic]"]
  C7 = Electrolytic Capacitor [capacitance=1µF package="100 mil [THT, electrolytic]"]
  R4 = Resistor [tolerance=±5% resistance=20k package=THT]
  J8 = female pin header, 2 pins [form="♀ (female)"]
  J9 = female pin header, 2 pins [form="♀ (female)"]  # not connected
  J10 = female pin header, 2 pins [form="♀ (female)"]
  J11 = female pin header, 3 pins [form="♀ (female)"]
  J12 = female pin header, 3 pins [form="♀ (female)"]  # not connected
  J13 = female pin header, 3 pins [form="♀ (female)"]
  J14 = female pin header, 2 pins [form="♀ (female)"]  # not connected
  R9 = Rotary Potentiometer (Small) [maximum_resistance=100kΩ package=THT]

nets:
  N1: IC1.A_OUT, R1.Pin_0, R4.Pin_1
  N2: IC1.A_-IN, R1.Pin_1, R2.Pin_0
  N3: IC1.A_+IN, IC1.B_+IN, R5.Pin_1, Q2.C, IC2.A_+IN, IC2.B_+IN, C2.0, C3.0, C4.0, C5.0, C6.-, C7.+, J13.pin2
  N4: IC1.A_V-, IC2.A_V-, C3.1, C5.1, C7.-, J13.pin3
  N5: IC1.B_-IN, IC1.B_OUT
  N6: IC1.A_V+, R6.Pin_0, IC2.A_V+, C2.1, C4.1, C6.+, J13.pin1
  N7: R5.Pin_0, Q1.C, R4.Pin_0
  N8: Q1.E, Q2.E, R7.Pin_1
  N9: Q1.B, R6.Pin_1, IC2.B_-IN, C1.1
  N10: Q2.B, R8.Pin_0
  N11: R7.Pin_0, IC2.B_OUT, C1.0
  N12: R8.Pin_1, J10.pin1
  N13: IC2.A_OUT, IC2.A_-IN
  N14: J8.pin1, R9.leg2
  N15: J8.pin2, R9.wiper
  N16: J11.pin2, J11.pin3

notes:
  VEE
  GND
  GND
  VCC
  2SC1815
  E / C / B
  Arduino LFO
  PCM5102A
  Function Generator
  +/-9V PSU
  OUT
  Current Source
  Select
  (External)
  TLF01
  Q Ctrl
  10k / B
