# Fritzing sketch TLF01+Antilog_ MiniMoog (saved by Fritzing 0.9.3b)
breadboards: 1
perfboards: 1

parts:
  Q1 = NPN-Transistor [package="TO92 [THT]"]
  Q2 = PNP-Transistor [package="TO92 [THT]"]
  R1 = Resistor [tolerance=±5% resistance=47k package=THT]
  R2 = Resistor [tolerance=±5% resistance=4.7k package=THT]
  R3 = Resistor [tolerance=±5% resistance=330 package=THT]
  R4 = Resistor [tolerance=±5% resistance=68k package=THT]
  R5 = Resistor [tolerance=±5% resistance=10k package=THT]
  C1 = Electrolytic Capacitor [capacitance=1µF package="100 mil [THT, electrolytic]"]
  R6 = TRIMPOT [package=trimpot_pth_s3_lock]
  J1 = female pin header, 2 pins [form="♀ (female)"]
  J2 = female pin header, 2 pins [form="♀ (female)"]  # not connected
  J3 = female pin header, 2 pins [form="♀ (female)"]
  J4 = female pin header, 3 pins [form="♀ (female)"]
  R7 = Resistor [tolerance=±5% resistance=1k package=THT]
  J5 = female pin header, 3 pins [form="♀ (female)"]
  J6 = female pin header, 3 pins [form="♀ (female)"]  # not connected
  J7 = female pin header, 2 pins [form="♀ (female)"]  # not connected
  R8 = Rotary Potentiometer (Small) [maximum_resistance=100kΩ package=THT]

nets:
  N1: Q1.E, R2.Pin_1, R3.Pin_1, C1.-, R6.CCW, J5.pin2
  N2: Q1.B, R5.Pin_0, R7.Pin_1
  N3: Q1.C, Q2.E, R4.Pin_1
  N4: Q2.B, R3.Pin_0
  N5: Q2.C, R1.Pin_0, R2.Pin_0
  N6: R4.Pin_0, R6.WIPER
  N7: R5.Pin_1, C1.+, R6.CW, J5.pin1
  N8: J1.pin1, R8.leg2
  N9: J1.pin2, R8.wiper
  N10: J3.pin1, R7.Pin_0
  N11: J4.pin2, J4.pin3

notes:
  Arduino LFO
  GND
  VCC
  2SC1814 / 2SA1015
  E/C/B
  Antilog
  V->C Convertor
  (NPN+PNP)
  PCM5102A
  Function Generator
  +/-9V PSU
  GND
  +9V
  OUT
  Current Source
  Select
  (External)
  TLF01
  Q Ctrl
  10k / B
