# Fritzing sketch MoogLadder_CS_JFET_V2 (saved by Fritzing 0.9.3b)
breadboards: 2

parts:
  C1 = Electrolytic Capacitor [capacitance=1µF package="100 mil [THT, electrolytic]"]
  R1 = Resistor [tolerance=±5% resistance=1k package=THT]
  R2 = Resistor [tolerance=±5% resistance=200 package=THT]
  C2 = Electrolytic Capacitor [capacitance=1µF package="100 mil [THT, electrolytic]"]
  R3 = Resistor [tolerance=±5% resistance=1k package=THT]
  Q1 = NPN-Transistor [package="TO92 [THT]"]
  Q2 = NPN-Transistor [package="TO92 [THT]"]
  Q3 = NPN-Transistor [package="TO92 [THT]"]
  Q4 = NPN-Transistor [package="TO92 [THT]"]
  Q5 = NPN-Transistor [package="TO92 [THT]"]
  Q6 = NPN-Transistor [package="TO92 [THT]"]
  C3 = Ceramic Capacitor [capacitance=100nF package="100 mil [THT, multilayer]"]
  C4 = Ceramic Capacitor [capacitance=100nF package="100 mil [THT, multilayer]"]
  C5 = Ceramic Capacitor [capacitance=100nF package="100 mil [THT, multilayer]"]
  C6 = Ceramic Capacitor [capacitance=100nF package="100 mil [THT, multilayer]"]
  R4 = Resistor [tolerance=±5% resistance=150 package=THT]
  R5 = Resistor [tolerance=±5% resistance=150 package=THT]
  R6 = Resistor [tolerance=±5% resistance=150 package=THT]
  R7 = Resistor [tolerance=±5% resistance=150 package=THT]
  R8 = Resistor [tolerance=±5% resistance=220k package=THT]
  R9 = Resistor [tolerance=±5% resistance=330 package=THT]
  Q7 = NPN-Transistor [package="TO92 [THT]"]
  Q8 = NPN-Transistor [package="TO92 [THT]"]
  Q9 = NPN-Transistor [package="TO92 [THT]"]
  Q10 = NPN-Transistor [package="TO92 [THT]"]
  IC1 = Dual Op-Amp [package=dip08]
  R10 = Resistor [tolerance=±5% resistance=1k package=THT]
  R11 = Resistor [tolerance=±5% resistance=1k package=THT]
  R12 = Resistor [tolerance=±5% resistance=100k package=THT]
  R13 = Resistor [tolerance=±5% resistance=100k package=THT]
  C7 = Ceramic Capacitor [capacitance=100nF package="100 mil [THT, multilayer]"]
  C8 = Ceramic Capacitor [capacitance=100nF package="100 mil [THT, multilayer]"]
  C9 = Electrolytic Capacitor [capacitance=1µF package="100 mil [THT, electrolytic]"]
  C10 = Electrolytic Capacitor [capacitance=1µF package="100 mil [THT, electrolytic]"]
  C11 = Electrolytic Capacitor [capacitance=1µF package="100 mil [THT, electrolytic]"]
  R18 = Rotary Potentiometer (Small) [maximum_resistance=100kΩ package=THT]
  R19 = Rotary Potentiometer (Small) [maximum_resistance=100kΩ package=THT]
  Q11 = Basic FET N-Channel [package="TO220 [THT]"]
  R20 = TRIMPOT [package=trimpot_pth_s3_lock]
  R21 = Resistor [tolerance=±5% resistance=47k package=THT]
  R22 = Resistor [tolerance=±5% resistance=1k package=THT]
  LED1 = LED - 5mm [color="Red (633nm)" package="5 mm [THT]"]
  LED2 = LED - 5mm [color="Green (570nm)" package="5 mm [THT]"]
  R23 = Resistor [tolerance=±5% resistance=1k package=THT]
  R24 = Resistor [tolerance=±5% resistance=1k package=THT]

nets:
  N1: C1.+, R1.Pin_1
  N2: R1.Pin_0, R3.Pin_0, Q1.C
  N3: R2.Pin_0, C2.-, IC1.A_+IN, R13.Pin_0, C7.1, C8.0, C10.-, C11.+, R18.leg2, Q11.drain, LED1.cathode, R23.Pin_0
  N4: R2.Pin_1, C2.+, R3.Pin_1, R4.Pin_1, R9.Pin_1
  N5: Q1.E, Q2.E, R24.Pin_0
  N6: Q1.B, Q3.E, C3.0
  N7: Q2.B, C3.1, Q7.E
  N8: Q2.C, R20.WIPER
  N9: Q3.B, Q4.E, C4.0
  N10: Q3.C, R4.Pin_0, R5.Pin_1, Q7.C
  N11: Q4.B, Q5.E, C5.0
  N12: Q4.C, R5.Pin_0, R6.Pin_1, Q8.C
  N13: Q5.B, Q6.E, C6.0, R10.Pin_1
  N14: Q5.C, R6.Pin_0, R7.Pin_1, Q9.C
  N15: Q6.B, R8.Pin_0, Q10.B, IC1.A_V+, C7.0, C10.+, R22.Pin_0
  N16: Q6.C, R7.Pin_0, R8.Pin_1, Q10.C
  N17: C4.1, Q7.B, Q8.E
  N18: C5.1, Q8.B, Q9.E
  N19: C6.1, Q9.B, Q10.E, R11.Pin_1
  N20: R9.Pin_0, R20.CCW
  N21: IC1.A_OUT, IC1.A_-IN
  N22: IC1.A_V-, C8.1
  N23: IC1.B_+IN, R11.Pin_0, R13.Pin_1
  N24: IC1.B_-IN, R10.Pin_0, R12.Pin_0
  N25: IC1.B_OUT, R12.Pin_1, C9.-
  N26: C9.+, R19.leg2
  N27: C11.-, LED2.cathode
  N28: R18.leg1, R18.wiper, R21.Pin_1
  N29: R19.leg1, R19.wiper, R20.CW
  N30: Q11.gate, R24.Pin_1
  N31: Q11.source, R21.Pin_0
  N32: R22.Pin_1, LED1.anode
  N33: LED2.anode, R23.Pin_1

notes:
  VEE
  GND
  WaveIn
  GND
  VCC
  2SC1815
  E / C / B
  586mV x 10
  Filter Out
  2SK170GR
  D / G / S
  50k/B
  1k/A
  GND
  NC
  1kΩ Trim
