# Fritzing sketch TLF01結線図 (saved by Fritzing 0.9.3b)
perfboards: 1

parts:
  J1 = female pin header, 2 pins [form="♀ (female)"]  # not connected
  J2 = female pin header, 2 pins [form="♀ (female)"]  # not connected
  J3 = female pin header, 2 pins [form="♀ (female)"]
  J4 = female pin header, 2 pins [form="♀ (female)"]  # not connected
  J5 = female pin header, 2 pins [form="♀ (female)"]
  J6 = female pin header, 2 pins [form="♀ (female)"]  # not connected
  J7 = female pin header, 2 pins [form="♀ (female)"]  # not connected
  J8 = female pin header, 3 pins [form="♀ (female)"]  # not connected
  J9 = female pin header, 3 pins [form="♀ (female)"]  # not connected
  R1 = Rotary Potentiometer (Small) [maximum_resistance=100kΩ package=THT]
  R2 = Rotary Potentiometer (Small) [maximum_resistance=100kΩ package=THT]
  J10 = female pin header, 3 pins [form="♀ (female)"]

nets:
  N1: J3.pin1, R2.leg1
  N2: J3.pin2, R2.wiper
  N3: J5.pin1, R1.wiper
  N4: J5.pin2, R1.leg1
  N5: J10.pin1, J10.pin2

notes:
  IN
  OUT
  +/- 9V PSU
  Q Ctrl
  Cutoff
  Ext Current
  Source
  (Sink)(Option)
  EXT PWR
  TLF01
  Current Source
  Select
  (Internal)
